# Fritzing sketch CARRT (saved by Fritzing 0.9.3b)
stripboards: 4
perfboards: 4

parts:
  Part1 = Arduino Mega 2560 (Rev3)
  LSM303DLHC = IC, DIP package, 16 pins [chip_label=LSM303DLHC]
  IC1 = IC, DIP package, 18 pins [chip_label=L3GD20]
  Part2 = 16-Channel 12-bit PCA9685 PWM/Servo Driver
  LCD1 = Adafruit Positive RGB 2x16 LCD
  IC2 = MCP23017 I2C I/O Expander
  S1 = Pushbutton [package="[SMD]"]
  S2 = Pushbutton [package="[SMD]"]
  S3 = Pushbutton [package="[SMD]"]
  S4 = Pushbutton [package="[SMD]"]
  S5 = Pushbutton [package="[SMD]"]
  S6 = Pushbutton [package="[SMD]"]
  R1 = Trimmer Potentiometer [maximum_resistance=10kΩ package=THT]  # not connected
  U1 = TMP36 [package=to-92]
  J5 = Basic Servo
  J6 = Infrared Proximity Sensor
  J7 = Piezo Speaker
  J8 = Screw terminal - 2 pins [package=THT]
  J9 = Screw terminal - 2 pins [package=THT]
  VCC1 = Battery
  VCC2 = Battery
  VCC3 = Battery
  VCC4 = Battery
  VCC5 = Battery
  BAT1 = Battery Holders [package=battery-aa-kit]
  J10 = Screw terminal - 2 pins [package=THT]
  J11 = Screw terminal - 2 pins [package=THT]
  J12 = Screw terminal - 2 pins [package=THT]
  J13 = Screw terminal - 2 pins [package=THT]
  J14 = Screw terminal - 2 pins [package=THT]
  M1 = DC Motor
  M2 = DC Motor
  M3 = DC Motor
  M4 = DC Motor
  LED1 = LED - 5mm [color="Red (633nm)" package="5 mm [THT]"]
  LED2 = LED - 5mm [color="Red (633nm)" package="5 mm [THT]"]
  LED3 = LED - 5mm [color="Yellow (585nm)" package="5 mm [THT]"]
  LED4 = LED - 5mm [color="Green (555nm)" package="5 mm [THT]"]
  LED5 = LED - 5mm [color="Yellow (585nm)" package="5 mm [THT]"]
  LED6 = LED - 5mm [color="Green (555nm)" package="5 mm [THT]"]
  R2 = Resistor [tolerance=±5% resistance=330 package=THT]
  R3 = Resistor [tolerance=±5% resistance=330 package=THT]
  R4 = Resistor [tolerance=±5% resistance=330 package=THT]
  R5 = Resistor [tolerance=±5% resistance=330 package=THT]
  R6 = Resistor [tolerance=±5% resistance=330 package=THT]
  R7 = Resistor [tolerance=±5% resistance=330 package=THT]
  U2 = SWITCH-SPST-2 [package=switch-spst-vertical]
  U3 = SWITCH-SPST-2 [package=switch-spst-vertical]
  R8 = Resistor [tolerance=±5% resistance=2.2k package=THT]
  R9 = Resistor [tolerance=±5% resistance=2.2k package=THT]
  R10 = Resistor [tolerance=±5% resistance=18k package=THT]
  R11 = Resistor [tolerance=±5% resistance=18k package=THT]
  C1 = Electrolytic Capacitor [capacitance=680µF voltage=5V package="100 mil [THT, electrolytic]"]

nets:
  N1: Part1.A0, R9.Pin_1, R11.Pin_0
  N2: Part1.A1, R8.Pin_1, R10.Pin_0
  N3: Part1.A2, U1.VOUT
  N4: Part1.D21/SCL, LSM303DLHC.pin1, IC1.pin1, Part2.SCL
  N5: Part1.D20/SDA, LSM303DLHC.pin2, IC1.pin2, Part2.SDA
  N6: Part1.D13_PWM, J7.pin2
  VCC: Part1.5V, LSM303DLHC.pin7, IC1.pin9, Part2.VCC, U1.VCC, J6.Vcc, C1.+
  GND: Part1.GND, LSM303DLHC.pin6, IC1.pin7, Part2.GND, U1.GND, J5.gnd, J6.GND, J7.pin1, J8.pin1, J9.pin2, VCC1.-, VCC2.-, VCC3.-, VCC4.-, VCC5.-, BAT1.-, J10.pin2, R2.Pin_1, R3.Pin_1, R4.Pin_1, R5.Pin_1, R6.Pin_1, R7.Pin_1, R8.Pin_0, R9.Pin_0, C1.-
  N7: Part1.VIN, J9.pin1, U2.P, R10.Pin_1
  N8: Part1.D22, LED6.anode
  N9: Part1.D23, LED4.anode
  N10: Part1.D24, LED5.anode
  N11: Part1.D25, LED3.anode
  N12: Part1.D26, LED2.anode
  N13: Part1.D27, LED1.anode
  N14: Part1.D29, J6.Vout
  N15: Part2.PWRIN, J10.pin1, U3.P, R11.Pin_1
  N16: Part2.0, J5.pulse
  N17: Part2.V+, J5.vcc
  N18: LCD1.no_name_yet#5, IC2.GPB6
  N19: LCD1.no_name_yet#6, IC2.VDD
  N20: LCD1.no_name_yet#15, S1.Pin_3, S1.Pin_4
  N21: S2.Pin_1, S2.Pin_2
  N22: S2.Pin_3, S2.Pin_4
  N23: S3.Pin_1, S3.Pin_2
  N24: S3.Pin_3, S3.Pin_4
  N25: S4.Pin_1, S4.Pin_2
  N26: S4.Pin_3, S4.Pin_4
  N27: S5.Pin_1, S5.Pin_2
  N28: S5.Pin_3, S5.Pin_4
  N29: S6.Pin_1, S6.Pin_2
  N30: S6.Pin_3, S6.Pin_4
  N31: J8.pin2, VCC1.+, VCC2.+, VCC3.+, U2.O
  N32: VCC4.+, VCC5.+, BAT1.+, U3.O
  N33: J11.pin1, M3.pin_2
  N34: J11.pin2, M3.pin_1
  N35: J12.pin1, M1.pin_2
  N36: J12.pin2, M1.pin_1
  N37: J13.pin1, M2.pin_2
  N38: J13.pin2, M2.pin_1
  N39: J14.pin1, M4.pin_2
  N40: J14.pin2, M4.pin_1
  N41: LED1.cathode, R2.Pin_0
  N42: LED2.cathode, R5.Pin_0
  N43: LED3.cathode, R3.Pin_0
  N44: LED4.cathode, R4.Pin_0
  N45: LED5.cathode, R7.Pin_0
  N46: LED6.cathode, R6.Pin_0

notes:
  AdaFruit Motor Board
  Lidar
  UltraSonic

custom parts:
  16-Channel 12-bit PCA9685 PWM/Servo Driver: The Adafruit 16-Channel 12-bit PWM/Servo Driver will drive up to 16 servos over I2C with only 2 pins. The on-board PCA9685 PWM controller will drive all 16 channels simultaneously with no additional processing overhead. What's more, you can chain up to 62 of them to control up to 992 servos - all with the same 2 pins
  Adafruit Positive RGB 2x16 LCD: Adafruit Positive 2x16 LCD Display with RGB Backlight
  MCP23017 I2C I/O Expander: The MCP23017 uses two i2c pins (these can be shared with other i2c devices), and in exchange gives you 16 general purpose pins. You can set each of 16 pins to be input, output, input with a pullup or open drain. There's even the ability to get an interrupt via an external pin when any of the inputs change so you don't have to keep polling the chip.
